// Logisim project feataku.circ as structural Verilog: 3 circuits, main circuit main
module main (
  input  in_1,
  input  [2:0] in_2,
  input  in_3,
  output out_4
);

  wire AND1, AND2, nor_1_out, nor_2_out;

  Demultiplexer #(.select(3), .enable("false")) demultiplexer_1 (
    .out0(AND1), .in(in_1), .sel(in_2));  // open: out1, out2, out3, out4, out5, out6, out7
  Demultiplexer #(.select(3), .enable("false")) demultiplexer_2 (
    .out0(AND2), .in(in_3), .sel(in_2));  // open: out1, out2, out3, out4, out5, out6, out7
  nor nor_1 (nor_1_out, AND1, AND1);
  nor nor_2 (nor_2_out, AND2, AND2);
  nor nor_3 (out_4, nor_1_out, nor_2_out);
endmodule

// SC
module SemiSumador (
  input  X,
  input  Y,
  input  CIn,
  output S,
  output COut
);

  wire and_1_out, and_2_out, xor_1_out;

  xor xor_1 (xor_1_out, X, Y);
  and and_1 (and_1_out, X, Y);
  xor xor_2 (S, xor_1_out, CIn);
  and and_2 (and_2_out, xor_1_out, CIn);
  xor xor_3 (COut, and_2_out, and_1_out);
endmodule

module Sumador4Bits (
  input  in_1,
  input  in_2,
  input  in_3,
  input  in_4,
  input  in_5,
  input  in_6,
  input  in_7,
  input  in_8,
  input  in_9,
  output out_10,
  output out_11,
  output out_12,
  output out_13,
  output out_14
);

  wire semisumador_1_cout, semisumador_2_cout, semisumador_3_cout;

  SemiSumador semisumador_1 (.X(in_1), .Y(in_2), .CIn(in_3), .S(out_10), .COut(semisumador_1_cout));
  SemiSumador semisumador_2 (.X(in_4), .Y(in_5), .CIn(semisumador_1_cout), .S(out_11), .COut(semisumador_2_cout));
  SemiSumador semisumador_3 (.X(in_6), .Y(in_7), .CIn(semisumador_2_cout), .S(out_12), .COut(semisumador_3_cout));
  SemiSumador semisumador_4 (.X(in_8), .Y(in_9), .CIn(semisumador_3_cout), .S(out_13), .COut(out_14));
endmodule
